// Logisim project A2.circ as structural Verilog
module main (
  input  [1:0] Address,
  input  [3:0] Data,
  input  in_3,
  output [3:0] Output
);

  wire _00_out, _0_q, _0W_out, _01_out, _1_q, _1W_out, _2_q, _2W_out, _3_q, _3W_out, _10_out, _11_out,
       ADDR_Register_q, and_1_out, and_2_out, and_3_out, and_4_out, and_5_out, and_6_out, and_7_out,
       and_8_out, and_9_out, and_10_out, and_11_out, and_12_out, and_13_out, and_14_out, and_15_out,
       and_16_out, and_17_out, and_18_out, and_19_out, and_20_out, and_21_out, and_22_out, and_23_out,
       and_24_out, and_25_out, and_26_out, and_27_out, and_28_out, and_29_out, and_30_out, and_31_out,
       and_32_out, and_33_out, and_34_out, and_35_out, and_36_out, and_37_out, and_38_out, and_39_out,
       and_40_out, and_41_out, and_42_out, and_43_out, and_44_out, and_45_out, and_46_out, and_47_out,
       and_48_out, and_49_out, and_50_out, and_51_out, and_52_out, and_53_out, and_54_out, and_55_out,
       and_56_out, clock_1_out, d_ff_1_q, d_ff_2_q, d_ff_3_q, d_ff_4_q, d_ff_5_q, d_ff_6_q, d_ff_7_q,
       d_ff_8_q, d_ff_9_q, d_ff_10_q, d_ff_11_q, d_ff_12_q, d_ff_13_q, d_ff_14_q, d_ff_15_q, d_ff_16_q,
       d_ff_17_q, Mode_Register_q, not_1_out, not_2_out, not_3_out, not_4_out, not_5_out, not_6_out,
       or_1_out, or_2_out, or_3_out, or_4_out, or_5_out, or_6_out, or_7_out, or_8_out, or_9_out, or_10_out,
       or_11_out, or_12_out, or_13_out, or_14_out, or_15_out, or_16_out;

  D_Flip_Flop ADDR_Register (.clk(clock_1_out), .D(Address[0]), .Q(ADDR_Register_q));  // open: Qn, preset, en, reset
  D_Flip_Flop d_ff_1 (.clk(clock_1_out), .D(Address[1]), .Q(d_ff_1_q));  // open: Qn, preset, en, reset
  not not_1 (not_1_out, ADDR_Register_q);
  not not_2 (not_2_out, d_ff_1_q);
  not not_3 (not_3_out, d_ff_1_q);
  not not_4 (not_4_out, ADDR_Register_q);
  and and_1 (and_1_out, Mode_Register_q, Data[2]);
  and and_2 (and_2_out, not_6_out, or_15_out);
  and and_3 (and_3_out, Mode_Register_q, Data[3]);
  or or_1 (or_1_out, and_3_out, and_4_out);
  and and_4 (and_4_out, not_6_out, or_16_out);
  and _00 (_00_out, not_1_out, not_2_out);
  and _01 (_01_out, ADDR_Register_q, not_3_out);
  and _10 (_10_out, not_4_out, d_ff_1_q);
  and _11 (_11_out, ADDR_Register_q, d_ff_1_q);
  D_Flip_Flop Mode_Register (.clk(clock_1_out), .D(in_3), .Q(Mode_Register_q));  // open: Qn, preset, en, reset
  D_Flip_Flop _2 (.clk(clock_1_out), .D(or_2_out), .Q(_2_q));  // open: Qn, preset, en, reset
  or or_2 (or_2_out, and_1_out, and_2_out);
  D_Flip_Flop _3 (.clk(clock_1_out), .D(or_1_out), .Q(_3_q));  // open: Qn, preset, en, reset
  not not_5 (not_5_out, Mode_Register_q);
  and and_5 (and_5_out, _0W_out, _00_out);
  and and_6 (and_6_out, _1W_out, _00_out);
  and and_7 (and_7_out, _2W_out, _00_out);
  and and_8 (and_8_out, _3W_out, _00_out);
  and and_9 (and_9_out, _1W_out, _01_out);
  and and_10 (and_10_out, _2W_out, _01_out);
  and and_11 (and_11_out, _3W_out, _01_out);
  Clock clock_1 (.out(clock_1_out));
  not not_6 (not_6_out, Mode_Register_q);
  and and_12 (and_12_out, Data[0], Mode_Register_q);
  and and_13 (and_13_out, or_13_out, not_6_out);
  and and_14 (and_14_out, Mode_Register_q, Data[1]);
  and and_15 (and_15_out, not_6_out, or_14_out);
  and and_16 (and_16_out, _0W_out, _01_out);
  and and_17 (and_17_out, _0W_out, _10_out);
  and and_18 (and_18_out, _1W_out, _10_out);
  and and_19 (and_19_out, _2W_out, _10_out);
  and and_20 (and_20_out, _3W_out, _10_out);
  and and_21 (and_21_out, _0W_out, _11_out);
  and and_22 (and_22_out, _1W_out, _11_out);
  and and_23 (and_23_out, _2W_out, _11_out);
  and and_24 (and_24_out, _3W_out, _11_out);
  or or_3 (or_3_out, and_12_out, and_13_out);
  or or_4 (or_4_out, and_14_out, and_15_out);
  D_Flip_Flop d_ff_2 (.clk(and_25_out), .D(and_5_out), .Q(d_ff_2_q));  // open: Qn, preset, en, reset
  and and_25 (and_25_out, clock_1_out, _00_out, Mode_Register_q);
  D_Flip_Flop d_ff_3 (.clk(and_26_out), .D(and_6_out), .Q(d_ff_3_q));  // open: Qn, preset, en, reset
  and and_26 (and_26_out, clock_1_out, _00_out, Mode_Register_q);
  and and_27 (and_27_out, clock_1_out, _00_out, Mode_Register_q);
  D_Flip_Flop d_ff_4 (.clk(and_27_out), .D(and_7_out), .Q(d_ff_4_q));  // open: Qn, preset, en, reset
  D_Flip_Flop d_ff_5 (.clk(and_28_out), .D(and_8_out), .Q(d_ff_5_q));  // open: Qn, preset, en, reset
  and and_28 (and_28_out, clock_1_out, _00_out, Mode_Register_q);
  D_Flip_Flop d_ff_6 (.clk(and_29_out), .D(and_16_out), .Q(d_ff_6_q));  // open: Qn, preset, en, reset
  and and_29 (and_29_out, clock_1_out, _01_out, Mode_Register_q);
  D_Flip_Flop d_ff_7 (.clk(and_30_out), .D(and_9_out), .Q(d_ff_7_q));  // open: Qn, preset, en, reset
  and and_30 (and_30_out, clock_1_out, _01_out, Mode_Register_q);
  and and_31 (and_31_out, clock_1_out, _01_out, Mode_Register_q);
  D_Flip_Flop d_ff_8 (.clk(and_31_out), .D(and_10_out), .Q(d_ff_8_q));  // open: Qn, preset, en, reset
  D_Flip_Flop d_ff_9 (.clk(and_32_out), .D(and_11_out), .Q(d_ff_9_q));  // open: Qn, preset, en, reset
  and and_32 (and_32_out, clock_1_out, _01_out, Mode_Register_q);
  D_Flip_Flop d_ff_10 (.clk(and_33_out), .D(and_17_out), .Q(d_ff_10_q));  // open: Qn, preset, en, reset
  and and_33 (and_33_out, _10_out, clock_1_out, Mode_Register_q);
  and and_34 (and_34_out, _10_out, clock_1_out, Mode_Register_q);
  D_Flip_Flop d_ff_11 (.clk(and_34_out), .D(and_18_out), .Q(d_ff_11_q));  // open: Qn, preset, en, reset
  D_Flip_Flop d_ff_12 (.clk(and_35_out), .D(and_19_out), .Q(d_ff_12_q));  // open: Qn, preset, en, reset
  and and_35 (and_35_out, _10_out, Mode_Register_q, clock_1_out);
  and and_36 (and_36_out, _10_out, clock_1_out, Mode_Register_q);
  D_Flip_Flop d_ff_13 (.clk(and_36_out), .D(and_20_out), .Q(d_ff_13_q));  // open: Qn, preset, en, reset
  and and_37 (and_37_out, _11_out, clock_1_out, Mode_Register_q);
  D_Flip_Flop d_ff_14 (.clk(and_37_out), .D(and_21_out), .Q(d_ff_14_q));  // open: Qn, preset, en, reset
  D_Flip_Flop d_ff_15 (.clk(and_38_out), .D(and_22_out), .Q(d_ff_15_q));  // open: Qn, preset, en, reset
  and and_38 (and_38_out, _11_out, Mode_Register_q, clock_1_out);
  and and_39 (and_39_out, _11_out, Mode_Register_q, clock_1_out);
  D_Flip_Flop d_ff_16 (.clk(and_39_out), .D(and_23_out), .Q(d_ff_16_q));  // open: Qn, preset, en, reset
  D_Flip_Flop d_ff_17 (.clk(and_40_out), .D(and_24_out), .Q(d_ff_17_q));  // open: Qn, preset, en, reset
  and and_40 (and_40_out, _11_out, Mode_Register_q, clock_1_out);
  D_Flip_Flop _0 (.clk(clock_1_out), .D(or_3_out), .Q(_0_q));  // open: Qn, preset, en, reset
  D_Flip_Flop _1 (.clk(clock_1_out), .D(or_4_out), .Q(_1_q));  // open: Qn, preset, en, reset
  and _1W (_1W_out, Mode_Register_q, _1_q);
  and and_41 (and_41_out, _00_out, d_ff_3_q, not_5_out);
  and and_42 (and_42_out, _00_out, d_ff_4_q, not_5_out);
  and and_43 (and_43_out, _00_out, d_ff_5_q, not_5_out);
  and and_44 (and_44_out, _01_out, d_ff_6_q, not_5_out);
  and and_45 (and_45_out, _01_out, d_ff_7_q, not_5_out);
  and and_46 (and_46_out, _01_out, d_ff_8_q, not_5_out);
  and and_47 (and_47_out, _01_out, d_ff_9_q, not_5_out);
  and and_48 (and_48_out, _10_out, d_ff_10_q, not_5_out);
  and and_49 (and_49_out, _10_out, d_ff_11_q, not_5_out);
  and and_50 (and_50_out, _10_out, d_ff_12_q, not_5_out);
  and and_51 (and_51_out, _10_out, d_ff_13_q, not_5_out);
  and and_52 (and_52_out, _11_out, d_ff_14_q, not_5_out);
  and and_53 (and_53_out, _11_out, d_ff_15_q, not_5_out);
  and and_54 (and_54_out, _11_out, d_ff_16_q, not_5_out);
  and _0W (_0W_out, _0_q, Mode_Register_q);
  and and_55 (and_55_out, _00_out, not_5_out, d_ff_2_q);
  and and_56 (and_56_out, _11_out, d_ff_17_q, not_5_out);
  and _3R (Output[3], not_6_out, _3_q);
  and _3W (_3W_out, _3_q, Mode_Register_q);
  and _2W (_2W_out, _2_q, Mode_Register_q);
  or or_5 (or_5_out, and_44_out, or_9_out);
  or or_6 (or_6_out, and_45_out, or_10_out);
  or or_7 (or_7_out, or_11_out, and_46_out);
  or or_8 (or_8_out, or_12_out, and_47_out);
  or or_9 (or_9_out, and_48_out, and_52_out);
  or or_10 (or_10_out, and_49_out, and_53_out);
  or or_11 (or_11_out, and_54_out, and_50_out);
  or or_12 (or_12_out, and_56_out, and_51_out);
  and _0R (Output[0], not_6_out, _0_q);
  and _1R (Output[1], not_6_out, _1_q);
  and _2R (Output[2], not_6_out, _2_q);
  or or_13 (or_13_out, and_55_out, or_5_out);
  or or_14 (or_14_out, and_41_out, or_6_out);
  or or_15 (or_15_out, or_7_out, and_42_out);
  or or_16 (or_16_out, or_8_out, and_43_out);

  // Notes on the sheet:
  //   Mode (1=write,0=read)
  //   Clock
  //   DO NOT MOVE the inputs, outputs or clock, Anything else can be moved.
endmodule
