// Logisim project assignment3.circ as structural Verilog: 4 circuits, main circuit main
module main (
  input  _3__highest_bit,
  input  _2,
  input  _1,
  input  _0,
  input  _3__highest,
  input  _2_2,
  input  _1_2,
  input  _0__lowest,
  input  Mode,
  output Overflow,
  output Overflow__Signed,
  output Zero,
  output Negative,
  output out_14,
  output out_15,
  output out_16,
  output out_17
);

  wire and_1_out, and_2_out, and_3_out, and_4_out, and_5_out, clock_1_out, d_ff_1_q, d_ff_2_q, d_ff_3_q,
       d_ff_4_q, d_ff_5_q, d_ff_6_q, d_ff_8_q, d_ff_10_q, fulladd1bit_1_carry, fulladd1bit_1_sum,
       fulladd1bit_2_carry, fulladd1bit_2_sum, fulladd1bit_3_carry, fulladd1bit_3_sum, fulladd1bit_4_carry,
       fulladd1bit_4_sum, not_1_out, not_2_out, not_3_out, not_4_out, not_5_out, not_6_out, not_7_out,
       not_8_out, not_9_out, not_10_out, not_11_out, not_12_out, xor_1_out;
  wire [3:0] n2scomplement_1_output, xor_2_out;

  D_Flip_Flop d_ff_1 (.clk(clock_1_out), .D(_0), .Q(d_ff_1_q));  // open: Qn, preset, en, reset
  ExactlyOne xor_1 (.out(xor_1_out), .in0(and_1_out), .in1(and_2_out), .in2(and_3_out), .in4(and_4_out));
  xor xor_2 (xor_2_out[0], Mode, d_ff_1_q);
  D_Flip_Flop d_ff_2 (.clk(clock_1_out), .D(_1), .Q(d_ff_2_q));  // open: Qn, preset, en, reset
  xor xor_3 (xor_2_out[1], Mode, d_ff_2_q);
  and and_1 (and_1_out, not_1_out, d_ff_4_q, fulladd1bit_4_sum, Mode);
  and and_2 (and_2_out, d_ff_10_q, Mode, not_2_out, not_3_out);
  and and_3 (and_3_out, fulladd1bit_4_sum, not_4_out, not_5_out, not_6_out);
  and and_4 (and_4_out, not_7_out, not_8_out, d_ff_4_q, d_ff_10_q);
  D_Flip_Flop d_ff_3 (.clk(clock_1_out), .D(_2), .Q(d_ff_3_q));  // open: Qn, preset, en, reset
  xor xor_4 (xor_2_out[2], Mode, d_ff_3_q);
  _2scomplement u_2scomplement_1 (.Input(xor_2_out), .Mode(Mode), .Output(n2scomplement_1_output));  // open: Carry
  not not_1 (not_1_out, d_ff_10_q);
  not not_2 (not_2_out, d_ff_4_q);
  not not_3 (not_3_out, fulladd1bit_4_sum);
  not not_4 (not_4_out, Mode);
  not not_5 (not_5_out, d_ff_4_q);
  not not_6 (not_6_out, d_ff_10_q);
  not not_7 (not_7_out, fulladd1bit_4_sum);
  not not_8 (not_8_out, Mode);
  D_Flip_Flop d_ff_4 (.clk(clock_1_out), .D(_3__highest_bit), .Q(d_ff_4_q));  // open: Qn, preset, en, reset
  xor xor_5 (xor_2_out[3], Mode, d_ff_4_q);
  Clock clock_1 (.out(clock_1_out));
  D_Flip_Flop d_ff_5 (.clk(clock_1_out), .D(_0__lowest), .Q(d_ff_5_q));  // open: Qn, preset, en, reset
  fulladd1bit fulladd1bit_1 (
    .a(d_ff_5_q), .b(n2scomplement_1_output[0]), .carryin(1'b0), .sum(fulladd1bit_1_sum),
    .carry(fulladd1bit_1_carry));
  D_Flip_Flop d_ff_6 (.clk(clock_1_out), .D(_1_2), .Q(d_ff_6_q));  // open: Qn, preset, en, reset
  fulladd1bit fulladd1bit_2 (
    .a(d_ff_6_q), .b(n2scomplement_1_output[1]), .carryin(fulladd1bit_1_carry), .sum(fulladd1bit_2_sum),
    .carry(fulladd1bit_2_carry));
  D_Flip_Flop d_ff_7 (.clk(clock_1_out), .D(fulladd1bit_1_sum), .Q(out_17));  // open: Qn, preset, en, reset
  D_Flip_Flop d_ff_8 (.clk(clock_1_out), .D(_2_2), .Q(d_ff_8_q));  // open: Qn, preset, en, reset
  fulladd1bit fulladd1bit_3 (
    .a(d_ff_8_q), .b(n2scomplement_1_output[2]), .carryin(fulladd1bit_2_carry), .sum(fulladd1bit_3_sum),
    .carry(fulladd1bit_3_carry));
  D_Flip_Flop d_ff_9 (.clk(clock_1_out), .D(fulladd1bit_2_sum), .Q(out_16));  // open: Qn, preset, en, reset
  D_Flip_Flop d_ff_10 (.clk(clock_1_out), .D(_3__highest), .Q(d_ff_10_q));  // open: Qn, preset, en, reset
  D_Flip_Flop d_ff_11 (.clk(clock_1_out), .D(fulladd1bit_3_sum), .Q(out_15));  // open: Qn, preset, en, reset
  fulladd1bit fulladd1bit_4 (
    .a(d_ff_10_q), .b(n2scomplement_1_output[3]), .carryin(fulladd1bit_3_carry), .sum(fulladd1bit_4_sum),
    .carry(fulladd1bit_4_carry));
  not not_9 (not_9_out, fulladd1bit_4_sum);
  not not_10 (not_10_out, fulladd1bit_3_sum);
  not not_11 (not_11_out, fulladd1bit_2_sum);
  not not_12 (not_12_out, fulladd1bit_1_sum);
  D_Flip_Flop d_ff_12 (.clk(clock_1_out), .D(fulladd1bit_4_sum), .Q(out_14));  // open: Qn, preset, en, reset
  and and_5 (and_5_out, not_9_out, not_10_out, not_11_out, not_12_out);
  D_Flip_Flop d_ff_13 (.clk(clock_1_out), .D(fulladd1bit_4_carry), .Q(Overflow));  // open: Qn, preset, en, reset
  D_Flip_Flop d_ff_14 (.clk(clock_1_out), .D(xor_1_out), .Q(Overflow__Signed));  // open: Qn, preset, en, reset
  D_Flip_Flop d_ff_15 (.clk(clock_1_out), .D(and_5_out), .Q(Zero));  // open: Qn, preset, en, reset
  D_Flip_Flop d_ff_16 (.clk(clock_1_out), .D(fulladd1bit_4_sum), .Q(Negative));  // open: Qn, preset, en, reset

  // Notes on the sheet:
  //   4 cases for a signed overflow 
  //   Right (addand)
  //   Left (input number)
endmodule

module fulladd1bit (
  input  a,
  input  b,
  input  carryin,
  output sum,
  output carry
);

  wire and_1_out, and_2_out, xor_1_out;

  and and_1 (and_1_out, a, b);
  xor xor_1 (xor_1_out, a, b);
  xor xor_2 (sum, xor_1_out, carryin);
  and and_2 (and_2_out, carryin, xor_1_out);
  or or_1 (carry, and_2_out, and_1_out);
endmodule

module _2scomplement (
  input  [3:0] Input,
  input  Mode,
  output [3:0] Output,
  output Carry
);

  wire half_adder_1_carry, half_adder_2_carry, half_adder_3_carry;

  Half_Adder half_adder_1 (.A(Input[0]), .B(Mode), .SUM(Output[0]), .CARRY(half_adder_1_carry));
  Half_Adder half_adder_2 (.A(half_adder_1_carry), .B(Input[1]), .SUM(Output[1]), .CARRY(half_adder_2_carry));
  Half_Adder half_adder_3 (.A(half_adder_2_carry), .B(Input[2]), .SUM(Output[2]), .CARRY(half_adder_3_carry));
  Half_Adder half_adder_4 (.A(half_adder_3_carry), .B(Input[3]), .SUM(Output[3]), .CARRY(Carry));
endmodule

module Half_Adder (
  input  A,
  input  B,
  output SUM,
  output CARRY
);

  xor xor_1 (SUM, A, B);
  and and_1 (CARRY, A, B);
endmodule
