// Logisim project A4.circ as structural Verilog: 2 circuits, main circuit main
module main (
  input  Op_Code,
  input  [1:0] R1,
  input  [1:0] R2,
  input  [1:0] R3
);

  wire and_2_out, and_3_out, clock_1_out, cu_1_merge1, cu_1_merge2, cu_1_move1, cu_1_move2, cu_1_stop,
       not_1_out, not_2_out, not_3_out, not_4_out, not_5_out, not_6_out, not_7_out, not_8_out, not_9_out,
       not_10_out, not_11_out, not_12_out, not_13_out, not_14_out, not_15_out, not_16_out, or_1_out, or_4_out;
  wire [2:0] adder_1_out, register_1_q, register_2_q;
  wire [3:0] and_15_out, and_16_out, and_17_out, and_18_out, and_19_out, and_20_out, and_21_out, and_22_out,
       and_23_out, or_2_out, or_5_out, or_6_out, or_7_out, or_8_out, or_9_out, Register_A_q, Register_B_q,
       Register_C_q;
  wire [3:3] and_4_out, and_5_out, and_6_out, and_7_out, and_8_out, and_9_out, and_10_out, and_11_out,
       and_12_out;
  wire [6:0] register_3_q;
  wire [7:0] and_13_out, and_14_out, or_3_out, register_4_q, TEMP_q;
  wire [7:7] and_1_out, cu_1_merge3;

  Clock clock_1 (.out(clock_1_out));
  Register #(.width(3)) register_1 (.D(adder_1_out), .Q(register_1_q), .clk(or_1_out));  // open: en, clr
  CU cu_1 (
    .in_1(register_3_q[0]), .in_2(register_3_q[2:1]), .counter(register_2_q), .MOVE1(cu_1_move1),
    .MOVE2(cu_1_move2), .MERGE1(cu_1_merge1), .MERGE2(cu_1_merge2), .MERGE3(cu_1_merge3[7]), .STOP(cu_1_stop));
  Register #(.width(3)) register_2 (.D(register_1_q), .Q(register_2_q), .clk(or_1_out));  // open: en, clr
  or or_1 (or_1_out, clock_1_out, cu_1_stop);
  Adder #(.width(3)) adder_1 (.a(register_2_q), .b(3'b001), .out(adder_1_out));  // open: cin, cout
  Register #(.width(7)) register_3 (.D({R3, R2, R1, Op_Code}), .Q(register_3_q), .clk(clock_1_out));  // open: en, clr
  not not_1 (not_1_out, register_3_q[1]);
  not not_2 (not_2_out, register_3_q[2]);
  not not_3 (not_3_out, register_3_q[2]);
  not not_4 (not_4_out, register_3_q[1]);
  not not_5 (not_5_out, register_3_q[3]);
  not not_6 (not_6_out, register_3_q[4]);
  not not_7 (not_7_out, register_3_q[4]);
  not not_8 (not_8_out, register_3_q[3]);
  not not_9 (not_9_out, register_3_q[3]);
  not not_10 (not_10_out, register_3_q[4]);
  not not_11 (not_11_out, register_3_q[4]);
  not not_12 (not_12_out, register_3_q[3]);
  not not_13 (not_13_out, register_3_q[5]);
  not not_14 (not_14_out, register_3_q[6]);
  not not_15 (not_15_out, register_3_q[6]);
  not not_16 (not_16_out, register_3_q[5]);
  and and_1 (and_1_out[7], cu_1_move2, not_1_out, not_2_out);
  and and_2 (and_2_out, cu_1_move2, register_3_q[1], not_3_out);
  and and_3 (and_3_out, cu_1_move2, not_4_out, register_3_q[2]);
  and and_4 (and_4_out[3], cu_1_move1, not_5_out, not_6_out);
  and and_5 (and_5_out[3], cu_1_move1, register_3_q[3], not_7_out);
  and and_6 (and_6_out[3], cu_1_move1, not_8_out, register_3_q[4]);
  and and_7 (and_7_out[3], cu_1_merge1, not_9_out, not_10_out);
  and and_8 (and_8_out[3], cu_1_merge1, register_3_q[3], not_11_out);
  and and_9 (and_9_out[3], cu_1_merge1, not_12_out, register_3_q[4]);
  and and_10 (and_10_out[3], cu_1_merge1, not_13_out, not_14_out);
  and and_11 (and_11_out[3], cu_1_merge1, register_3_q[5], not_15_out);
  and and_12 (and_12_out[3], cu_1_merge1, not_16_out, register_3_q[6]);
  assign and_13_out = TEMP_q & {8{cu_1_merge3[7]}};  // AND_Gate and_13, 8 bits wide
  assign and_14_out = register_4_q & {8{and_1_out[7]}};  // AND_Gate and_14, 8 bits wide
  assign and_15_out = Register_A_q & {4{and_4_out[3]}};  // AND_Gate and_15, 4 bits wide
  assign and_16_out = Register_B_q & {4{and_5_out[3]}};  // AND_Gate and_16, 4 bits wide
  assign or_2_out = and_16_out | and_15_out;  // OR_Gate or_2, 4 bits wide
  assign and_17_out = {4{and_6_out[3]}} & Register_C_q;  // AND_Gate and_17, 4 bits wide
  assign or_3_out = and_13_out | and_14_out;  // OR_Gate or_3, 8 bits wide
  or or_4 (or_4_out, cu_1_merge3[7], and_1_out[7]);
  assign or_5_out = or_2_out | and_17_out;  // OR_Gate or_5, 4 bits wide
  Register #(.trigger("falling")) Register_A (
    .D(or_3_out), .Q({register_4_q[7:4], Register_A_q}), .clk(or_4_out));  // open: en, clr
  Register #(.width(4)) Register_B (.D(register_4_q[3:0]), .Q(Register_B_q), .clk(and_2_out));  // open: en, clr
  Register #(.width(4)) Register_C (.D(register_4_q[3:0]), .Q(Register_C_q), .clk(and_3_out));  // open: en, clr
  assign and_18_out = Register_A_q & {4{and_7_out[3]}};  // AND_Gate and_18, 4 bits wide
  assign and_19_out = Register_B_q & {4{and_8_out[3]}};  // AND_Gate and_19, 4 bits wide
  assign and_20_out = {4{and_9_out[3]}} & Register_C_q;  // AND_Gate and_20, 4 bits wide
  assign and_21_out = Register_A_q & {4{and_10_out[3]}};  // AND_Gate and_21, 4 bits wide
  assign and_22_out = Register_B_q & {4{and_11_out[3]}};  // AND_Gate and_22, 4 bits wide
  assign and_23_out = {4{and_12_out[3]}} & Register_C_q;  // AND_Gate and_23, 4 bits wide
  assign or_6_out = and_19_out | and_18_out;  // OR_Gate or_6, 4 bits wide
  assign or_7_out = or_6_out | and_20_out;  // OR_Gate or_7, 4 bits wide
  assign or_8_out = and_21_out | or_9_out;  // OR_Gate or_8, 4 bits wide
  Register TEMP (.D({or_7_out, or_8_out}), .Q(TEMP_q), .clk(cu_1_merge2));  // open: en, clr
  assign or_9_out = and_22_out | and_23_out;  // OR_Gate or_9, 4 bits wide
  Register #(.width(4)) register_4 (.D(or_5_out), .Q(register_4_q[3:0]), .clk(cu_1_move2));  // open: en, clr

  // Notes on the sheet:
  //   USE THE POKE TOOL to input the bits into the register. OPCODE:0=MOVE 1=MERGE
endmodule

module CU (
  input  in_1,
  input  [1:0] in_2,
  input  [2:0] counter,
  output MOVE1,
  output MOVE2,
  output MERGE1,
  output MERGE2,
  output MERGE3,
  output STOP
);

  wire _000_out, _001_out, _010_out, _011_out, and_1_out, and_2_out, and_3_out, and_4_out, not_1_out,
       not_2_out, not_3_out, not_4_out, not_5_out, not_6_out, not_7_out, not_8_out, not_9_out, not_10_out,
       not_11_out, not_12_out, not_13_out;

  and and_1 (and_1_out, in_1, and_2_out);
  and and_2 (and_2_out, ~in_2[1], ~in_2[0]);  // AND_Gate
  and and_3 (and_3_out, counter[0], counter[1], and_1_out);
  and and_4 (and_4_out, ~counter[0], ~counter[1], counter[2], not_1_out);  // AND_Gate
  not not_1 (not_1_out, and_1_out);
  not not_2 (not_2_out, counter[0]);
  not not_3 (not_3_out, counter[1]);
  and _000 (_000_out, not_2_out, not_3_out, not_4_out);
  not not_4 (not_4_out, and_1_out);
  and _001 (_001_out, counter[0], not_5_out, not_6_out);
  not not_5 (not_5_out, counter[1]);
  not not_6 (not_6_out, and_1_out);
  not not_7 (not_7_out, counter[0]);
  and _010 (_010_out, not_7_out, counter[1], not_8_out);
  not not_8 (not_8_out, and_1_out);
  not not_9 (not_9_out, counter[0]);
  not not_10 (not_10_out, counter[1]);
  and _100 (MERGE1, not_9_out, not_10_out, and_1_out);
  and _101 (MERGE2, counter[0], not_11_out, and_1_out);
  not not_11 (not_11_out, counter[1]);
  not not_12 (not_12_out, counter[0]);
  and _110 (MERGE3, not_12_out, counter[1], and_1_out);
  or or_1 (STOP, and_3_out, and_4_out);
  and _011 (_011_out, counter[0], counter[1], not_13_out);
  not not_13 (not_13_out, and_1_out);
  or or_2 (MOVE1, _000_out, _010_out);
  or or_3 (MOVE2, _001_out, _011_out);
endmodule
